# Fritzing sketch Schematic (saved by Fritzing 0.9.3b)
breadboards: 1

parts:
  U1 = NodeMCU V1.0
  Part2 = GUVA-S12SD UV Light Sensor

nets:
  GND: U1.GND, Part2.GND
  3V3: U1.3V3, Part2.5V
  N1: U1.A0, Part2.Out

notes:
  2.2K

custom parts:
  NodeMCU V1.0: ESP8266 based NodeMCU
  GUVA-S12SD UV Light Sensor: Extend your light-sensing spectrum with this analog UV sensor module. It uses a UV photodiode, which can detect the 240-370nm range of light (which covers UVB and most of UVA spectrum). The signal level from the photodiode is very small, in the nano-ampere level, so we tossed on an opamp to amplify the signal to a more manageable volt-level.
