# Fritzing sketch Schematic (saved by Fritzing 0.9.3b)
breadboards: 1

parts:
  hc-sr1 = hc-sr04
  U1 = NodeMCU V1.0
  R1 = Resistor [tolerance=±5% resistance=220 package="1206 [SMD]"]
  R2 = Resistor [tolerance=±5% resistance=220 package="1206 [SMD]"]

nets:
  VCC: hc-sr1.VCC, U1.Vin
  N1: hc-sr1.Trig, U1.D5
  N2: hc-sr1.Echo, R1.Pin_0
  GND: hc-sr1.GND, U1.GND, R2.Pin_1
  N3: U1.D6, R1.Pin_1, R2.Pin_0

notes:
  Esp8266 has 3.3V tolerant pins. So we have connected Echo pin of HC SR-04 to Esp8266 digital pin D6 via resistor network formed using (2.2K and 4.7K).
  2.2K is connected to Echo pin and 4.7K is grounded.
  Ultrasonic Sensor
  HC SR-04 requires 5V Vcc to function
  2.2K
  4.7K

custom parts:
  NodeMCU V1.0: ESP8266 based NodeMCU
